// Logisim project CPU_FINAL (1).circ as structural Verilog: 13 circuits, main circuit Main Arq2
module banco_de_registradores (
  input  clear,
  input  [3:0] \SAÍDA_1 ,
  input  [3:0] \SAÍDA_2 ,
  input  [15:0] DATA,
  input  [2:0] ESCRITA,
  input  RegWrite,
  input  CLOCK,
  output [15:0] RT,
  output [15:0] RS,
  output [15:0] RD
);

  wire and_1_out, and_2_out, and_3_out, and_4_out, and_5_out, and_6_out, and_7_out, and_8_out, reg1, reg2,
       reg3, reg4, reg5, reg6, reg7, reg8;
  wire [15:0] RB, saida1, saida2, saida3, saida4, saida5, saida6, saida7, saida8;

  Decoder #(.select(3)) decoder_1 (
    .out0(reg1), .out1(reg2), .out2(reg3), .out3(reg4), .out4(reg5), .out5(reg6), .out6(reg7), .out7(reg8),
    .sel(ESCRITA));  // open: en
  and and_1 (and_1_out, reg1, RegWrite);
  and and_2 (and_2_out, reg2, RegWrite);
  and and_3 (and_3_out, reg3, RegWrite);
  and and_4 (and_4_out, reg4, RegWrite);
  and and_5 (and_5_out, reg5, RegWrite);
  and and_6 (and_6_out, reg6, RegWrite);
  and and_7 (and_7_out, reg7, RegWrite);
  and and_8 (and_8_out, reg8, RegWrite);
  Register #(.width(16)) register_1 (.D(DATA), .en(and_1_out), .Q(saida1), .clk(CLOCK), .clr(clear));
  Register #(.width(16)) register_2 (.D(DATA), .en(and_2_out), .Q(saida2), .clk(CLOCK), .clr(clear));
  Register #(.width(16)) register_3 (.D(DATA), .en(and_3_out), .Q(saida3), .clk(CLOCK), .clr(clear));
  Register #(.width(16)) register_4 (.D(DATA), .en(and_4_out), .Q(saida4), .clk(CLOCK), .clr(clear));
  Register #(.width(16)) register_5 (.D(DATA), .en(and_5_out), .Q(saida5), .clk(CLOCK), .clr(clear));
  Register #(.width(16)) register_6 (.D(DATA), .en(and_6_out), .Q(saida6), .clk(CLOCK), .clr(clear));
  Register #(.width(16)) register_7 (.D(DATA), .en(and_7_out), .Q(saida7), .clk(CLOCK), .clr(clear));
  Register #(.width(16)) register_8 (.D(DATA), .en(and_8_out), .Q(saida8), .clk(CLOCK), .clr(clear));
  Register #(.width(16)) register_9 (.D({16{1'b0}}), .Q(RB), .clk(CLOCK), .clr(clear));  // open: en
  Multiplexer #(.select(4), .width(16)) multiplexer_1 (
    .in0(saida1), .in1(saida2), .in2(saida3), .in3(saida4), .in4(saida5), .in5(saida6), .in6(saida7),
    .in7(saida8), .in8(RB), .out(RT), .sel(\SAÍDA_1 ));  // open: in9, in10, in11, in12, in13, in14, in15, en
  Multiplexer #(.select(4), .width(16)) multiplexer_2 (
    .in0(saida1), .in1(saida2), .in2(saida3), .in3(saida4), .in4(saida5), .in5(saida6), .in6(saida7),
    .in7(saida8), .in8(RB), .out(RS), .sel(\SAÍDA_2 ));  // open: in9, in10, in11, in12, in13, in14, in15, en
  Multiplexer #(.select(3), .width(16)) multiplexer_3 (
    .in0(saida1), .in1(saida2), .in2(saida3), .in3(saida4), .in4(saida5), .in5(saida6), .in6(saida7),
    .in7(saida8), .out(RD), .sel(ESCRITA));  // open: en

  // Other names for the same wires on the sheet: leitor1[3:0] = \SAÍDA_1 ; leitor2[3:0] = \SAÍDA_2 ;
  //   seletor[2:0] = ESCRITA
endmodule

module processador_arq2 (
  input  [15:0] LW,
  input  STALL,
  input  CLOCK,
  input  CLEAR,
  input  SELECT,
  input  ENABLE,
  input  INSTRUCTIONS_ENABLE,
  input  start,
  input  MODIFICADO,
  output [15:0] SW,
  output memRead,
  output memWrite,
  output [9:0] ADDRESS,
  output clk_off
);

  wire ALUsrc, and_3_out, and_4_out, and_6_out, and_7_out, and_8_out, and_9_out, and_10_out, and_11_out, BEQ,
       BIT_6, Branch, comparator_1_eq, I_FILTER, JUMP, multiplexer_2_out, multiplexer_8_out,
       multiplexer_10_out, not_1_out, not_2_out, not_3_out, not_4_out, not_5_out, or_1_out, or_2_out,
       or_3_out, or_4_out, or_5_out, or_6_out, RBsignal, register_1_q, RegWrite, stall_2, TIPO_I, TIPO_R,
       writing, wrote;
  wire [0:0] demultiplexer_2_out0;
  wire [1:0] ALUop;
  wire [2:0] OPCODE;
  wire [3:0] bit_extender_4_out, RT;
  wire [9:0] bit_extender_1_out, bit_extender_2_out;
  wire [12:0] J;
  wire [15:0] adder_1_out, adder_2_out, bit_extender_3_out, DADOS, IMM, \INSTRUÇÃO , LW_t, multiplexer_3_out,
       multiplexer_4_out, multiplexer_5_out, multiplexer_11_out, multiplexer_12_out, multiplexer_13_out,
       multiplexer_14_out, PC, pc_t, SAIDA_RD, SAIDA_RS, SAIDA_RT;

  Comparator #(.width(16)) comparator_1 (.a(16'h81), .b(pc_t), .eq(comparator_1_eq));  // open: gt, lt
  Multiplexer multiplexer_1 (.in0(ENABLE), .in1(1'b0), .out(clk_off), .sel(comparator_1_eq));  // open: en
  Register #(.width(1)) register_1 (.D(STALL), .en(clk_off), .Q(register_1_q), .clk(CLOCK), .clr(CLEAR));
  and and_1 (writing, memWrite, ~MODIFICADO);  // AND_Gate
  and and_2 (stall_2, ~start, register_1_q);  // AND_Gate
  or or_1 (or_1_out, writing, STALL);
  not not_1 (not_1_out, or_1_out);
  Multiplexer multiplexer_2 (.in0(1'b0), .in1(clk_off), .out(multiplexer_2_out), .sel(not_1_out));  // open: en
  and and_3 (and_3_out, memRead, ~CLOCK);  // AND_Gate
  and and_4 (and_4_out, memRead, ~CLOCK);  // AND_Gate
  Multiplexer #(.width(16)) multiplexer_3 (.in0(PC), .in1(16'h6f), .out(multiplexer_3_out), .sel(start));  // open: en
  or or_2 (or_2_out, INSTRUCTIONS_ENABLE, and_3_out);
  Demultiplexer #(.width(16)) demultiplexer_1 (.out0(LW_t), .out1(\INSTRUÇÃO ), .in(LW), .sel(or_3_out));  // open: en
  or or_3 (or_3_out, INSTRUCTIONS_ENABLE, and_4_out);
  Register #(.width(16), .trigger("falling")) u_PC (
    .D(multiplexer_3_out), .en(multiplexer_2_out), .Q(pc_t), .clk(CLOCK), .clr(CLEAR));
  and and_5 (wrote, MODIFICADO, memWrite);
  or or_4 (or_4_out, or_2_out, wrote);
  Bit_Extender #(.in_width(16), .out_width(10)) bit_extender_1 (.in(pc_t), .out(bit_extender_1_out));
  Adder #(.width(16)) adder_1 (.a(SAIDA_RT), .b(IMM), .out(adder_1_out));  // open: cin, cout
  Multiplexer #(.width(16)) multiplexer_4 (
    .in0(adder_1_out), .in1(IMM), .out(multiplexer_4_out), .sel(I_FILTER));  // open: en
  Register #(.width(16)) register_2 (
    .D(\INSTRUÇÃO ), .en(or_4_out), .Q({OPCODE, J[12:7], BIT_6, J[5:0]}), .clk(CLOCK), .clr(CLEAR));
  Adder #(.width(16)) adder_2 (.a(16'h1), .b(pc_t), .out(adder_2_out));  // open: cin, cout
  and and_6 (and_6_out, BEQ, Branch);
  Bit_Extender #(.in_width(16), .out_width(10)) bit_extender_2 (.in(multiplexer_4_out), .out(bit_extender_2_out));
  assign SW = not_2_out ? SAIDA_RD : 16'bz;  // Controlled_Buffer controlled_buffer_1
  not not_2 (not_2_out, wrote);
  and and_7 (and_7_out, ~TIPO_R, ~TIPO_I, and_8_out);  // AND_Gate
  and and_8 (and_8_out, ~INSTRUCTIONS_ENABLE, ~start);  // AND_Gate
  Multiplexer #(.width(16)) multiplexer_5 (
    .in0(adder_2_out), .in1(IMM), .out(multiplexer_5_out), .sel(and_6_out));  // open: en
  or or_5 (or_5_out, and_7_out, memWrite, memRead);
  Demultiplexer demultiplexer_2 (
    .out0(demultiplexer_2_out0[0]), .out1(RBsignal), .in(BIT_6), .sel(Branch));  // open: en
  Multiplexer #(.width(16)) multiplexer_6 (
    .in0(multiplexer_5_out), .in1(bit_extender_3_out), .out(PC), .sel(JUMP));  // open: en
  assign bit_extender_3_out = {{3{1'b0}}, {J[12:7], BIT_6, J[5:0]}};  // Bit_Extender bit_extender_3
  or or_6 (or_6_out, and_9_out, writing);
  and and_9 (and_9_out, and_10_out, ~and_11_out, ~stall_2);  // AND_Gate
  and and_10 (and_10_out, ~wrote, or_5_out);  // AND_Gate
  and and_11 (and_11_out, memRead, ~CLOCK);  // AND_Gate
  Multiplexer #(.width(10)) multiplexer_7 (
    .in0(bit_extender_1_out), .in1(bit_extender_2_out), .out(ADDRESS), .sel(multiplexer_8_out));  // open: en
  Multiplexer multiplexer_8 (.in0(or_6_out), .in1(1'b0), .out(multiplexer_8_out), .sel(JUMP));  // open: en
  gambiarra_1 gambiarra_1_1 (.a(OPCODE[2]), .b(OPCODE[1]), .c(OPCODE[0]), .x(I_FILTER));
  unidade_de_controle_arq2 UC (
    .OPCODE(OPCODE), .RegWrite(RegWrite), .TIPO_I(TIPO_I), .ALUsrc(ALUsrc), .LW__MemRead(memRead),
    .SW__MemWrite(memWrite), .BEQ(Branch), .JMP(JUMP), .ALUop(ALUop), .TIPO_R(TIPO_R));
  assign bit_extender_4_out = {{1{1'b0}}, J[9:7]};  // Bit_Extender bit_extender_4
  Multiplexer #(.width(4)) multiplexer_9 (
    .in0(bit_extender_4_out), .in1({J[9:7], demultiplexer_2_out0[0]}), .out(RT), .sel(not_3_out));  // open: en
  not not_3 (not_3_out, Branch);
  assign IMM = {{9{1'b0}}, {RBsignal, J[5:0]}};  // Bit_Extender bit_extender_5
  Multiplexer multiplexer_10 (.in0(RegWrite), .in1(1'b0), .out(multiplexer_10_out), .sel(STALL));  // open: en
  Multiplexer #(.width(16)) multiplexer_11 (
    .in0(IMM), .in1(LW_t), .out(multiplexer_11_out), .sel(memRead));  // open: en
  Multiplexer #(.width(16)) multiplexer_12 (
    .in0(SAIDA_RS), .in1(multiplexer_11_out), .out(multiplexer_12_out), .sel(ALUsrc));  // open: en
  not not_4 (not_4_out, CLOCK);
  not not_5 (not_5_out, Branch);
  Multiplexer #(.width(16)) multiplexer_13 (
    .in0(SAIDA_RT), .in1(multiplexer_12_out), .out(multiplexer_13_out), .sel(not_5_out));  // open: en
  banco_de_registradores banco_de_registradores_1 (
    .clear(CLEAR), .\SAÍDA_1 (RT), .\SAÍDA_2 (J[3:0]), .DATA(DADOS), .ESCRITA(J[12:10]),
    .RegWrite(multiplexer_10_out), .CLOCK(not_4_out), .RT(SAIDA_RT), .RS(SAIDA_RS), .RD(SAIDA_RD));
  Multiplexer #(.width(16)) multiplexer_14 (
    .in0(SAIDA_RD), .in1(SAIDA_RT), .out(multiplexer_14_out), .sel(not_5_out));  // open: en
  ALU_arq_2 ALU (
    .ENTRADA_1(multiplexer_14_out), .ENTRADA_2(multiplexer_13_out), .ALUop(ALUop), .RESULTADO(DADOS),
    .out_5(BEQ));

  // Other names for the same wires on the sheet: ENABLE_t = clk_off; INS_FILTER = INSTRUCTIONS_ENABLE;
  //   MINI_IMM[6:0] = {BIT_6, J[5:0]}; RS[3:0] = J[3:0]; J[6] = BIT_6; RD[2:0] = J[12:10]

  // Notes on the sheet:
  //   CONTADOR DE PROGRAMA
  //   OPERAÇÕES DE DESVIOS
  //   RS
  //   RD
  //   RT
  //   IMM
  //   BANCO DE REGISTRADORES
endmodule

module unidade_de_controle_arq2 (
  input  [2:0] OPCODE,
  output RegWrite,
  output TIPO_I,
  output ALUsrc,
  output LW__MemRead,
  output SW__MemWrite,
  output BEQ,
  output JMP,
  output [1:0] ALUop,
  output TIPO_R
);

  wire and_1_out, and_2_out, and_3_out, and_4_out, and_9_out, and_10_out;

  and and_1 (and_1_out, ~OPCODE[0], ~OPCODE[1], ~OPCODE[2]);  // AND_Gate
  and and_2 (and_2_out, OPCODE[0], ~OPCODE[1], ~OPCODE[2]);  // AND_Gate
  and and_3 (and_3_out, ~OPCODE[0], OPCODE[1], ~OPCODE[2]);  // AND_Gate
  and and_4 (and_4_out, OPCODE[0], OPCODE[1], ~OPCODE[2]);  // AND_Gate
  and and_5 (LW__MemRead, ~OPCODE[0], ~OPCODE[1], OPCODE[2]);  // AND_Gate
  and and_6 (SW__MemWrite, OPCODE[0], ~OPCODE[1], OPCODE[2]);  // AND_Gate
  and and_7 (BEQ, ~OPCODE[0], OPCODE[1], OPCODE[2]);  // AND_Gate
  and and_8 (JMP, OPCODE[0], OPCODE[1], OPCODE[2]);
  gambiarra_2 gambiarra_2_1 (.a(OPCODE[2]), .b(OPCODE[1]), .c(OPCODE[0]), .x(ALUop[1]), .y(ALUop[0]));
  and and_9 (and_9_out, ~OPCODE[0], ~OPCODE[1], ~OPCODE[2]);  // AND_Gate
  and and_10 (and_10_out, ~OPCODE[0], OPCODE[1], OPCODE[2]);  // AND_Gate
  ExactlyOne xor_1 (.out(ALUsrc), .in0(and_3_out), .in1(and_4_out), .in2(LW__MemRead));
  or or_1 (TIPO_R, and_9_out, and_10_out);
  or or_2 (TIPO_I, and_3_out, and_4_out);
  or or_3 (RegWrite, and_1_out, and_2_out, ALUsrc);
endmodule

module ALU_arq_2 (
  input  [15:0] ENTRADA_1,
  input  [15:0] ENTRADA_2,
  input  [1:0] ALUop,
  output [15:0] RESULTADO,
  output out_5
);

  wire [15:0] adder_1_out, and_1_out;

  Adder #(.width(16)) adder_1 (.a(ENTRADA_1), .b(ENTRADA_2), .out(adder_1_out));  // open: cin, cout
  assign and_1_out = ENTRADA_1 & ENTRADA_2;  // AND_Gate and_1, 16 bits wide
  Comparator #(.width(16)) comparator_1 (.a(ENTRADA_1), .b(ENTRADA_2), .eq(out_5));  // open: gt, lt
  Multiplexer #(.select(2), .width(16)) multiplexer_1 (
    .in0(adder_1_out), .in1(and_1_out), .in2(ENTRADA_2), .out(RESULTADO), .sel(ALUop));  // open: in3, en

  // Other names for the same wires on the sheet: A[15:0] = ENTRADA_1; B[15:0] = ENTRADA_2
endmodule

module gambiarra_1 (
  input  a,
  input  b,
  input  c,
  output x
);

  wire and_1_out, and_2_out, not_1_out, not_2_out;

  not not_1 (not_1_out, a);
  not not_2 (not_2_out, c);
  and and_1 (and_1_out, not_1_out, b);
  and and_2 (and_2_out, b, not_2_out);
  or or_1 (x, and_1_out, and_2_out);
endmodule

module gambiarra_2 (
  input  a,
  input  b,
  input  c,
  output x,
  output y
);

  wire not_1_out, not_2_out;

  not not_1 (not_1_out, b);
  not not_2 (not_2_out, a);
  and and_1 (x, a, not_1_out);
  and and_2 (y, not_2_out, c);
endmodule

module cache (
  input  [9:0] ADDRESS,
  input  [15:0] _00,
  input  [15:0] _01,
  input  [15:0] _10,
  input  [15:0] _11,
  input  [15:0] DATA_TO_STORE,
  input  SW,
  input  LW,
  input  CLOCK,
  input  CLEAR,
  input  block_saved,
  output [9:0] address_to_write,
  output [15:0] _00_2,
  output [15:0] _01_2,
  output [15:0] _10_2,
  output [15:0] _11_2,
  output WRITE_BACK,
  output [15:0] DATA_TO_LOAD,
  output [9:0] out_19,
  output HIT,
  output \INSTRUÇÃO ,
  output MODIFIED
);

  wire and_1_out, and_2_out, and_3_out, and_4_out, and_5_out, and_6_out, and_7_out, and_8_out, and_17_out,
       and_18_out, and_19_out, and_20_out, and_21_out, and_22_out, and_23_out, and_24_out, and_25_out,
       and_26_out, and_27_out, and_28_out, and_29_out, and_30_out, and_31_out, and_32_out, and_49_out,
       and_50_out, and_51_out, and_52_out, and_53_out, and_54_out, and_55_out, and_56_out, and_57_out,
       and_58_out, and_59_out, and_60_out, and_61_out, and_62_out, and_63_out, and_64_out, and_65_out,
       and_66_out, and_67_out, and_68_out, and_69_out, comparator_1_eq, comparator_2_eq, comparator_3_eq,
       comparator_4_eq, comparator_5_eq, comparator_6_eq, comparator_7_eq, comparator_8_eq, comparator_9_eq,
       comparator_10_eq, comparator_11_eq, comparator_12_eq, comparator_13_eq, comparator_14_eq,
       comparator_15_eq, comparator_16_eq, EN_SET_1_LIN_1, EN_SET_1_LIN_2, EN_SET_2_LIN_1, EN_SET_2_LIN_2,
       EN_SET_3_LIN_1, EN_SET_3_LIN_2, EN_SET_4_LIN_1, EN_SET_4_LIN_2, INS_1_SET_1, INS_1_SET_2, INS_1_SET_3,
       INS_1_SET_4, INS_2_SET_1, INS_2_SET_2, INS_2_SET_3, INS_2_SET_4, ins_set_1, ins_set_2, ins_set_3,
       ins_set_4, instruction, LIN_1_SET_1_FILTER, LIN_1_SET_2_FILTER, LIN_1_SET_3_FILTER,
       LIN_1_SET_4_FILTER, LIN_2_SET_1_FILTER, LIN_2_SET_2_FILTER, LIN_2_SET_3_FILTER, LIN_2_SET_4_FILTER,
       LRU_1_SET_1, LRU_1_SET_2, LRU_1_SET_3, LRU_1_SET_4, LRU_2_SET_1, LRU_2_SET_2, LRU_2_SET_3,
       LRU_2_SET_4, M1_LIN_1, M1_LIN_2, M2_LIN_1, M2_LIN_2, M2_LIN_2_t, M3_LIN_1, M3_LIN_1_t, M3_LIN_2,
       M3_LIN_2_t, M4_LIN_1, M4_LIN_1_t, M4_LIN_2, M4_LIN_2_t, miss_1, miss_2, miss_3, miss_4,
       multiplexer_9_out, multiplexer_10_out, multiplexer_11_out, not_1_out, not_2_out, not_3_out, not_4_out,
       not_5_out, not_6_out, not_7_out, not_8_out, or_2_out, or_3_out, or_4_out, or_5_out, or_6_out,
       or_7_out, or_8_out, or_9_out, or_10_out, or_11_out, or_12_out, or_13_out, or_14_out, or_15_out,
       or_16_out, or_17_out, or_18_out, or_19_out, or_20_out, or_21_out, or_22_out, or_23_out, or_24_out,
       or_25_out, or_27_out, register_1_q, register_2_q, register_3_q, register_4_q, set1, set2, set3, set4,
       str_lin_1_set_1, str_lin_1_set_2, str_lin_1_set_3, str_lin_1_set_4, str_lin_2_set_1, str_lin_2_set_2,
       str_lin_2_set_3, str_lin_2_set_4, sw_set_1, sw_set_2, sw_set_3, sw_set_4, V1_1_SET_1, V1_1_SET_2,
       V1_1_SET_3, V1_1_SET_4, V2_1_SET_1, V2_1_SET_2, V2_1_SET_3, V2_1_SET_4, WAY_1_SET_1, WAY_1_SET_2,
       WAY_1_SET_3, WAY_1_SET_4, WAY_2_SET_1, WAY_2_SET_2, WAY_2_SET_3, WAY_2_SET_4;
  wire [1:0] INST;
  wire [5:0] controlled_buffer_1_out, controlled_buffer_2_out, controlled_buffer_3_out,
       controlled_buffer_4_out, controlled_buffer_5_out, controlled_buffer_6_out, controlled_buffer_7_out,
       controlled_buffer_8_out, TAG_1_SET_1, TAG_1_SET_2, TAG_1_SET_3, TAG_1_SET_4, TAG_2_SET_1, TAG_2_SET_2,
       TAG_2_SET_3, TAG_2_SET_4, TAG_SET_1, TAG_SET_2, TAG_SET_3, TAG_SET_4;
  wire [15:0] linha_cache_1__00, linha_cache_1__01, linha_cache_1__10, linha_cache_1__11, linha_cache_2__00,
       linha_cache_2__01, linha_cache_2__10, linha_cache_2__11, linha_cache_3__00, linha_cache_3__01,
       linha_cache_3__10, linha_cache_3__11, linha_cache_4__00, linha_cache_4__01, linha_cache_4__10,
       linha_cache_4__11, linha_cache_5__00, linha_cache_5__01, linha_cache_5__10, linha_cache_5__11,
       linha_cache_6__00, linha_cache_6__01, linha_cache_6__10, linha_cache_6__11, linha_cache_7__00,
       linha_cache_7__01, linha_cache_7__10, linha_cache_7__11, linha_cache_8__00, linha_cache_8__01,
       linha_cache_8__10, linha_cache_8__11, set_1, SET_1_00, SET_1_01, SET_1_10, SET_1_11, set_2, SET_2_00,
       SET_2_01, SET_2_10, SET_2_11, set_3, SET_3_00, SET_3_01, SET_3_10, SET_3_11, set_4, SET_4_00,
       SET_4_01, SET_4_10, SET_4_11, WORD_1_SET_1, WORD_1_SET_2, WORD_1_SET_3, WORD_1_SET_4, WORD_2_SET_1,
       WORD_2_SET_2, WORD_2_SET_3, WORD_2_SET_4;

  Decoder #(.select(2)) decoder_1 (.out0(set1), .out1(set2), .out2(set3), .out3(set4), .sel(ADDRESS[3:2]));  // open: en
  or or_1 (instruction, ADDRESS[5], ADDRESS[6], ADDRESS[7], ADDRESS[8], ADDRESS[9]);
  LRU lru_1 (
    .V1(V1_1_SET_1), .V2(V2_1_SET_1), .LRU_1(LRU_1_SET_1), .LRU_2(LRU_2_SET_1), .MISS(miss_1),
    .memWrite(and_1_out), .WAY_1(WAY_1_SET_1), .WAY_2(WAY_2_SET_1), .SW(sw_set_1));
  and and_1 (and_1_out, set1, register_1_q);
  or or_2 (or_2_out, block_saved, ~HIT);  // OR_Gate
  LRU lru_2 (
    .V1(V1_1_SET_2), .V2(V2_1_SET_2), .LRU_1(LRU_1_SET_2), .LRU_2(LRU_2_SET_2), .MISS(miss_2),
    .memWrite(and_2_out), .WAY_1(WAY_1_SET_2), .WAY_2(WAY_2_SET_2), .SW(sw_set_2));
  and and_2 (and_2_out, set2, register_2_q);
  or or_3 (or_3_out, block_saved, ~HIT);  // OR_Gate
  LRU lru_3 (
    .V1(V1_1_SET_3), .V2(V2_1_SET_3), .LRU_1(LRU_1_SET_3), .LRU_2(LRU_2_SET_3), .MISS(miss_3),
    .memWrite(and_3_out), .WAY_1(WAY_1_SET_3), .WAY_2(WAY_2_SET_3), .SW(sw_set_3));
  and and_3 (and_3_out, set3, register_3_q);
  or or_4 (or_4_out, block_saved, ~HIT);  // OR_Gate
  LRU lru_4 (
    .V1(V1_1_SET_4), .V2(V2_1_SET_4), .LRU_1(LRU_1_SET_4), .LRU_2(LRU_2_SET_4), .MISS(miss_4),
    .memWrite(and_7_out), .WAY_1(WAY_1_SET_4), .WAY_2(WAY_2_SET_4), .SW(sw_set_4));
  Register #(.width(1)) register_1 (.D(block_saved), .en(or_2_out), .Q(register_1_q), .clk(CLOCK), .clr(and_4_out));
  and and_4 (and_4_out, ~miss_1, or_8_out);  // AND_Gate
  Register #(.width(1)) register_2 (.D(block_saved), .en(or_3_out), .Q(register_2_q), .clk(CLOCK), .clr(and_5_out));
  and and_5 (and_5_out, ~miss_2, or_6_out);  // AND_Gate
  Register #(.width(1)) register_3 (.D(block_saved), .en(or_4_out), .Q(register_3_q), .clk(CLOCK), .clr(and_6_out));
  and and_6 (and_6_out, ~miss_3, or_7_out);  // AND_Gate
  and and_7 (and_7_out, set4, register_4_q);
  or or_5 (or_5_out, block_saved, ~HIT);  // OR_Gate
  or or_6 (or_6_out, LW, instruction);
  or or_7 (or_7_out, LW, instruction);
  Register #(.width(1)) register_4 (.D(block_saved), .en(or_5_out), .Q(register_4_q), .clk(CLOCK), .clr(and_8_out));
  and and_8 (and_8_out, ~miss_4, or_9_out);  // AND_Gate
  or or_8 (or_8_out, LW, instruction);
  or or_9 (or_9_out, LW, instruction);
  and and_9 (EN_SET_1_LIN_1, set1, WAY_1_SET_1);
  and and_10 (EN_SET_1_LIN_2, set1, WAY_2_SET_1);
  and and_11 (EN_SET_2_LIN_1, set2, WAY_1_SET_2);
  and and_12 (EN_SET_2_LIN_2, set2, WAY_2_SET_2);
  and and_13 (EN_SET_3_LIN_1, set3, WAY_1_SET_3);
  and and_14 (EN_SET_3_LIN_2, set3, WAY_2_SET_3);
  and and_15 (EN_SET_4_LIN_1, set4, WAY_1_SET_4);
  and and_16 (EN_SET_4_LIN_2, set4, WAY_2_SET_4);
  not not_1 (not_1_out, WRITE_BACK);
  assign controlled_buffer_1_out = not_1_out ? ADDRESS[9:4] : 6'bz;  // Controlled_Buffer controlled_buffer_1
  and and_17 (and_17_out, sw_set_1, set1);
  not not_2 (not_2_out, WRITE_BACK);
  and and_18 (and_18_out, sw_set_2, set2);
  not not_3 (not_3_out, WRITE_BACK);
  assign controlled_buffer_2_out = not_3_out ? ADDRESS[9:4] : 6'bz;  // Controlled_Buffer controlled_buffer_2
  and and_19 (and_19_out, sw_set_2, set2);
  not not_4 (not_4_out, WRITE_BACK);
  assign controlled_buffer_3_out = not_4_out ? ADDRESS[9:4] : 6'bz;  // Controlled_Buffer controlled_buffer_3
  and and_20 (and_20_out, sw_set_3, set3);
  not not_5 (not_5_out, WRITE_BACK);
  assign controlled_buffer_4_out = not_5_out ? ADDRESS[9:4] : 6'bz;  // Controlled_Buffer controlled_buffer_4
  and and_21 (and_21_out, sw_set_3, set3);
  not not_6 (not_6_out, WRITE_BACK);
  assign controlled_buffer_5_out = not_6_out ? ADDRESS[9:4] : 6'bz;  // Controlled_Buffer controlled_buffer_5
  and and_22 (and_22_out, sw_set_4, set4);
  not not_7 (not_7_out, WRITE_BACK);
  assign controlled_buffer_6_out = not_7_out ? ADDRESS[9:4] : 6'bz;  // Controlled_Buffer controlled_buffer_6
  and and_23 (and_23_out, sw_set_4, set4);
  and and_24 (and_24_out, sw_set_1, set1);
  not not_8 (not_8_out, WRITE_BACK);
  assign controlled_buffer_7_out = not_8_out ? ADDRESS[9:4] : 6'bz;  // Controlled_Buffer controlled_buffer_7
  assign controlled_buffer_8_out = not_2_out ? ADDRESS[9:4] : 6'bz;  // Controlled_Buffer controlled_buffer_8
  linha_cache linha_cache_1 (
    .data_00(_00), .data_01(_01), .data_10(_10), .data_11(_11), .WORD(DATA_TO_STORE), .offset(ADDRESS[1:0]),
    .tag(controlled_buffer_1_out), .SW(and_24_out), .clock(CLOCK), .enable(EN_SET_1_LIN_1),
    .LRU(WAY_1_SET_1), .CLEAR(CLEAR), .store_word(str_lin_1_set_1), .block_saved(and_25_out),
    .modificado(MODIFIED), ._00(linha_cache_1__00), ._01(linha_cache_1__01), ._10(linha_cache_1__10),
    ._11(linha_cache_1__11), .WORD_2(WORD_1_SET_1), .TAG_2(TAG_1_SET_1), .V(V1_1_SET_1), .M(M1_LIN_1),
    .LRU_2(LRU_1_SET_1), .\INSTRUÇÃO (INS_1_SET_1));
  and and_25 (and_25_out, block_saved, LIN_1_SET_1_FILTER);
  linha_cache linha_cache_2 (
    .data_00(_00), .data_01(_01), .data_10(_10), .data_11(_11), .WORD(DATA_TO_STORE), .offset(ADDRESS[1:0]),
    .tag(controlled_buffer_7_out), .SW(and_17_out), .clock(CLOCK), .enable(EN_SET_1_LIN_2),
    .LRU(WAY_2_SET_1), .CLEAR(CLEAR), .store_word(str_lin_2_set_1), .block_saved(and_26_out),
    .modificado(MODIFIED), ._00(linha_cache_2__00), ._01(linha_cache_2__01), ._10(linha_cache_2__10),
    ._11(linha_cache_2__11), .WORD_2(WORD_2_SET_1), .TAG_2(TAG_2_SET_1), .V(V2_1_SET_1), .M(M1_LIN_2),
    .LRU_2(LRU_2_SET_1), .\INSTRUÇÃO (INS_2_SET_1));
  and and_26 (and_26_out, block_saved, LIN_2_SET_1_FILTER);
  linha_cache linha_cache_3 (
    .data_00(_00), .data_01(_01), .data_10(_10), .data_11(_11), .WORD(DATA_TO_STORE), .offset(ADDRESS[1:0]),
    .tag(controlled_buffer_8_out), .SW(and_18_out), .clock(CLOCK), .enable(EN_SET_2_LIN_1),
    .LRU(WAY_1_SET_2), .CLEAR(CLEAR), .store_word(str_lin_1_set_2), .block_saved(and_27_out),
    .modificado(MODIFIED), ._00(linha_cache_3__00), ._01(linha_cache_3__01), ._10(linha_cache_3__10),
    ._11(linha_cache_3__11), .WORD_2(WORD_1_SET_2), .TAG_2(TAG_1_SET_2), .V(V1_1_SET_2), .M(M2_LIN_1),
    .LRU_2(LRU_1_SET_2), .\INSTRUÇÃO (INS_1_SET_2));
  and and_27 (and_27_out, block_saved, LIN_1_SET_2_FILTER);
  linha_cache linha_cache_4 (
    .data_00(_00), .data_01(_01), .data_10(_10), .data_11(_11), .WORD(DATA_TO_STORE), .offset(ADDRESS[1:0]),
    .tag(controlled_buffer_2_out), .SW(and_19_out), .clock(CLOCK), .enable(EN_SET_2_LIN_2),
    .LRU(WAY_2_SET_2), .CLEAR(CLEAR), .store_word(str_lin_2_set_2), .block_saved(and_28_out),
    .modificado(MODIFIED), ._00(linha_cache_4__00), ._01(linha_cache_4__01), ._10(linha_cache_4__10),
    ._11(linha_cache_4__11), .WORD_2(WORD_2_SET_2), .TAG_2(TAG_2_SET_2), .V(V2_1_SET_2), .M(M2_LIN_2_t),
    .LRU_2(LRU_2_SET_2), .\INSTRUÇÃO (INS_2_SET_2));
  and and_28 (and_28_out, block_saved, LIN_2_SET_2_FILTER);
  linha_cache linha_cache_5 (
    .data_00(_00), .data_01(_01), .data_10(_10), .data_11(_11), .WORD(DATA_TO_STORE), .offset(ADDRESS[1:0]),
    .tag(controlled_buffer_3_out), .SW(and_20_out), .clock(CLOCK), .enable(EN_SET_3_LIN_1),
    .LRU(WAY_1_SET_3), .CLEAR(CLEAR), .store_word(str_lin_1_set_3), .block_saved(and_29_out),
    .modificado(MODIFIED), ._00(linha_cache_5__00), ._01(linha_cache_5__01), ._10(linha_cache_5__10),
    ._11(linha_cache_5__11), .WORD_2(WORD_1_SET_3), .TAG_2(TAG_1_SET_3), .V(V1_1_SET_3), .M(M3_LIN_1_t),
    .LRU_2(LRU_1_SET_3), .\INSTRUÇÃO (INS_1_SET_3));
  and and_29 (and_29_out, block_saved, LIN_1_SET_3_FILTER);
  linha_cache linha_cache_6 (
    .data_00(_00), .data_01(_01), .data_10(_10), .data_11(_11), .WORD(DATA_TO_STORE), .offset(ADDRESS[1:0]),
    .tag(controlled_buffer_4_out), .SW(and_21_out), .clock(CLOCK), .enable(EN_SET_3_LIN_2),
    .LRU(WAY_2_SET_3), .CLEAR(CLEAR), .store_word(str_lin_2_set_3), .block_saved(and_30_out),
    .modificado(MODIFIED), ._00(linha_cache_6__00), ._01(linha_cache_6__01), ._10(linha_cache_6__10),
    ._11(linha_cache_6__11), .WORD_2(WORD_2_SET_3), .TAG_2(TAG_2_SET_3), .V(V2_1_SET_3), .M(M3_LIN_2_t),
    .LRU_2(LRU_2_SET_3), .\INSTRUÇÃO (INS_2_SET_3));
  and and_30 (and_30_out, block_saved, LIN_2_SET_3_FILTER);
  linha_cache linha_cache_7 (
    .data_00(_00), .data_01(_01), .data_10(_10), .data_11(_11), .WORD(DATA_TO_STORE), .offset(ADDRESS[1:0]),
    .tag(controlled_buffer_5_out), .SW(and_22_out), .clock(CLOCK), .enable(EN_SET_4_LIN_1),
    .LRU(WAY_1_SET_4), .CLEAR(CLEAR), .store_word(str_lin_1_set_4), .block_saved(and_31_out),
    .modificado(MODIFIED), ._00(linha_cache_7__00), ._01(linha_cache_7__01), ._10(linha_cache_7__10),
    ._11(linha_cache_7__11), .WORD_2(WORD_1_SET_4), .TAG_2(TAG_1_SET_4), .V(V1_1_SET_4), .M(M4_LIN_1_t),
    .LRU_2(LRU_1_SET_4), .\INSTRUÇÃO (INS_1_SET_4));
  and and_31 (and_31_out, block_saved, LIN_1_SET_4_FILTER);
  linha_cache linha_cache_8 (
    .data_00(_00), .data_01(_01), .data_10(_10), .data_11(_11), .WORD(DATA_TO_STORE), .offset(ADDRESS[1:0]),
    .tag(controlled_buffer_6_out), .SW(and_23_out), .clock(CLOCK), .enable(EN_SET_4_LIN_2),
    .LRU(WAY_2_SET_4), .CLEAR(CLEAR), .store_word(str_lin_2_set_4), .block_saved(and_32_out),
    .modificado(MODIFIED), ._00(linha_cache_8__00), ._01(linha_cache_8__01), ._10(linha_cache_8__10),
    ._11(linha_cache_8__11), .WORD_2(WORD_2_SET_4), .TAG_2(TAG_2_SET_4), .V(V2_1_SET_4), .M(M4_LIN_2_t),
    .LRU_2(LRU_2_SET_4), .\INSTRUÇÃO (INS_2_SET_4));
  and and_32 (and_32_out, block_saved, LIN_2_SET_4_FILTER);
  assign SET_1_00 = LIN_2_SET_1_FILTER ? linha_cache_2__00 : 16'bz;  // Controlled_Buffer controlled_buffer_9
  assign SET_1_01 = LIN_2_SET_1_FILTER ? linha_cache_2__01 : 16'bz;  // Controlled_Buffer controlled_buffer_10
  assign SET_1_10 = LIN_2_SET_1_FILTER ? linha_cache_2__10 : 16'bz;  // Controlled_Buffer controlled_buffer_11
  assign SET_1_11 = LIN_2_SET_1_FILTER ? linha_cache_2__11 : 16'bz;  // Controlled_Buffer controlled_buffer_12
  assign SET_2_00 = LIN_2_SET_2_FILTER ? linha_cache_4__00 : 16'bz;  // Controlled_Buffer controlled_buffer_13
  assign SET_2_01 = LIN_2_SET_2_FILTER ? linha_cache_4__01 : 16'bz;  // Controlled_Buffer controlled_buffer_14
  assign SET_2_10 = LIN_2_SET_2_FILTER ? linha_cache_4__10 : 16'bz;  // Controlled_Buffer controlled_buffer_15
  assign SET_2_11 = LIN_2_SET_2_FILTER ? linha_cache_4__11 : 16'bz;  // Controlled_Buffer controlled_buffer_16
  assign SET_3_00 = LIN_1_SET_3_FILTER ? linha_cache_5__00 : 16'bz;  // Controlled_Buffer controlled_buffer_17
  assign SET_3_01 = LIN_1_SET_3_FILTER ? linha_cache_5__01 : 16'bz;  // Controlled_Buffer controlled_buffer_18
  assign SET_3_10 = LIN_1_SET_3_FILTER ? linha_cache_5__10 : 16'bz;  // Controlled_Buffer controlled_buffer_19
  assign SET_3_11 = LIN_1_SET_3_FILTER ? linha_cache_5__11 : 16'bz;  // Controlled_Buffer controlled_buffer_20
  assign SET_3_00 = LIN_2_SET_3_FILTER ? linha_cache_6__00 : 16'bz;  // Controlled_Buffer controlled_buffer_21
  assign SET_3_01 = LIN_2_SET_3_FILTER ? linha_cache_6__01 : 16'bz;  // Controlled_Buffer controlled_buffer_22
  assign SET_3_10 = LIN_2_SET_3_FILTER ? linha_cache_6__10 : 16'bz;  // Controlled_Buffer controlled_buffer_23
  assign SET_3_11 = LIN_2_SET_3_FILTER ? linha_cache_6__11 : 16'bz;  // Controlled_Buffer controlled_buffer_24
  assign SET_4_00 = LIN_1_SET_4_FILTER ? linha_cache_7__00 : 16'bz;  // Controlled_Buffer controlled_buffer_25
  assign SET_4_01 = LIN_1_SET_4_FILTER ? linha_cache_7__01 : 16'bz;  // Controlled_Buffer controlled_buffer_26
  assign SET_4_10 = LIN_1_SET_4_FILTER ? linha_cache_7__10 : 16'bz;  // Controlled_Buffer controlled_buffer_27
  assign SET_4_11 = LIN_1_SET_4_FILTER ? linha_cache_7__11 : 16'bz;  // Controlled_Buffer controlled_buffer_28
  assign SET_4_00 = LIN_2_SET_4_FILTER ? linha_cache_8__00 : 16'bz;  // Controlled_Buffer controlled_buffer_29
  assign SET_4_01 = LIN_2_SET_4_FILTER ? linha_cache_8__01 : 16'bz;  // Controlled_Buffer controlled_buffer_30
  assign SET_4_10 = LIN_2_SET_4_FILTER ? linha_cache_8__10 : 16'bz;  // Controlled_Buffer controlled_buffer_31
  assign SET_4_11 = LIN_2_SET_4_FILTER ? linha_cache_8__11 : 16'bz;  // Controlled_Buffer controlled_buffer_32
  assign SET_1_00 = LIN_1_SET_1_FILTER ? linha_cache_1__00 : 16'bz;  // Controlled_Buffer controlled_buffer_33
  assign SET_1_01 = LIN_1_SET_1_FILTER ? linha_cache_1__01 : 16'bz;  // Controlled_Buffer controlled_buffer_34
  assign SET_1_10 = LIN_1_SET_1_FILTER ? linha_cache_1__10 : 16'bz;  // Controlled_Buffer controlled_buffer_35
  assign SET_1_11 = LIN_1_SET_1_FILTER ? linha_cache_1__11 : 16'bz;  // Controlled_Buffer controlled_buffer_36
  and and_33 (LIN_1_SET_1_FILTER, ~LRU_1_SET_1, M1_LIN_1);  // AND_Gate
  and and_34 (LIN_2_SET_1_FILTER, ~LRU_2_SET_1, M1_LIN_2);  // AND_Gate
  assign SET_2_00 = LIN_1_SET_2_FILTER ? linha_cache_3__00 : 16'bz;  // Controlled_Buffer controlled_buffer_37
  assign SET_2_01 = LIN_1_SET_2_FILTER ? linha_cache_3__01 : 16'bz;  // Controlled_Buffer controlled_buffer_38
  assign SET_2_10 = LIN_1_SET_2_FILTER ? linha_cache_3__10 : 16'bz;  // Controlled_Buffer controlled_buffer_39
  assign SET_2_11 = LIN_1_SET_2_FILTER ? linha_cache_3__11 : 16'bz;  // Controlled_Buffer controlled_buffer_40
  and and_35 (LIN_1_SET_2_FILTER, ~LRU_1_SET_2, M2_LIN_1);  // AND_Gate
  and and_36 (LIN_1_SET_3_FILTER, ~LRU_1_SET_3, M3_LIN_1_t);  // AND_Gate
  and and_37 (LIN_2_SET_3_FILTER, ~LRU_2_SET_3, M3_LIN_2_t);  // AND_Gate
  and and_38 (LIN_1_SET_4_FILTER, ~LRU_1_SET_4, M4_LIN_1_t);  // AND_Gate
  and and_39 (LIN_2_SET_4_FILTER, ~LRU_2_SET_4, M4_LIN_2_t);  // AND_Gate
  and and_40 (LIN_2_SET_2_FILTER, ~LRU_2_SET_2, M2_LIN_2_t);  // AND_Gate
  and and_41 (str_lin_1_set_1, SW, set1, comparator_1_eq);
  Comparator #(.width(6)) comparator_1 (.a(ADDRESS[9:4]), .b(TAG_1_SET_1), .eq(comparator_1_eq));  // open: gt, lt
  and and_42 (str_lin_2_set_1, SW, set1, comparator_2_eq);
  Comparator #(.width(6)) comparator_2 (.a(ADDRESS[9:4]), .b(TAG_2_SET_1), .eq(comparator_2_eq));  // open: gt, lt
  Comparator #(.width(6)) comparator_3 (.a(ADDRESS[9:4]), .b(TAG_1_SET_3), .eq(comparator_3_eq));  // open: gt, lt
  Comparator #(.width(6)) comparator_4 (.a(ADDRESS[9:4]), .b(TAG_2_SET_3), .eq(comparator_4_eq));  // open: gt, lt
  Comparator #(.width(6)) comparator_5 (.a(ADDRESS[9:4]), .b(TAG_2_SET_4), .eq(comparator_5_eq));  // open: gt, lt
  Comparator #(.width(6)) comparator_6 (.a(ADDRESS[9:4]), .b(TAG_1_SET_2), .eq(comparator_6_eq));  // open: gt, lt
  and and_43 (str_lin_2_set_2, SW, set2, comparator_7_eq);
  Comparator #(.width(6)) comparator_7 (.a(ADDRESS[9:4]), .b(TAG_2_SET_2), .eq(comparator_7_eq));  // open: gt, lt
  and and_44 (str_lin_1_set_3, SW, set3, comparator_3_eq);
  and and_45 (str_lin_2_set_3, SW, set3, comparator_4_eq);
  and and_46 (str_lin_1_set_4, SW, set4, comparator_8_eq);
  Comparator #(.width(6)) comparator_8 (.a(ADDRESS[9:4]), .b(TAG_1_SET_4), .eq(comparator_8_eq));  // open: gt, lt
  and and_47 (str_lin_2_set_4, SW, set4, comparator_5_eq);
  and and_48 (str_lin_1_set_2, SW, set2, comparator_6_eq);
  Comparator #(.width(6)) comparator_9 (.a(ADDRESS[9:4]), .b(TAG_1_SET_1), .eq(comparator_9_eq));  // open: gt, lt
  Comparator #(.width(6)) comparator_10 (.a(ADDRESS[9:4]), .b(TAG_2_SET_1), .eq(comparator_10_eq));  // open: gt, lt
  Comparator #(.width(6)) comparator_11 (.a(ADDRESS[9:4]), .b(TAG_1_SET_2), .eq(comparator_11_eq));  // open: gt, lt
  Comparator #(.width(6)) comparator_12 (.a(ADDRESS[9:4]), .b(TAG_2_SET_2), .eq(comparator_12_eq));  // open: gt, lt
  Comparator #(.width(6)) comparator_13 (.a(ADDRESS[9:4]), .b(TAG_1_SET_3), .eq(comparator_13_eq));  // open: gt, lt
  Comparator #(.width(6)) comparator_14 (.a(ADDRESS[9:4]), .b(TAG_2_SET_3), .eq(comparator_14_eq));  // open: gt, lt
  Comparator #(.width(6)) comparator_15 (.a(ADDRESS[9:4]), .b(TAG_1_SET_4), .eq(comparator_15_eq));  // open: gt, lt
  Comparator #(.width(6)) comparator_16 (.a(ADDRESS[9:4]), .b(TAG_2_SET_4), .eq(comparator_16_eq));  // open: gt, lt
  Multiplexer #(.select(2), .width(16)) multiplexer_1 (
    .in0(SET_1_00), .in1(SET_2_00), .in2(SET_3_00), .in3(SET_4_00), .out(_00_2), .sel(ADDRESS[3:2]));  // open: en
  Multiplexer #(.select(2), .width(16)) multiplexer_2 (
    .in0(SET_1_01), .in1(SET_2_01), .in2(SET_3_01), .in3(SET_4_01), .out(_01_2), .sel(ADDRESS[3:2]));  // open: en
  Multiplexer #(.select(2), .width(16)) multiplexer_3 (
    .in0(SET_1_10), .in1(SET_2_10), .in2(SET_3_10), .in3(SET_4_10), .out(_10_2), .sel(ADDRESS[3:2]));  // open: en
  Multiplexer #(.select(2), .width(16)) multiplexer_4 (
    .in0(SET_1_11), .in1(SET_2_11), .in2(SET_3_11), .in3(SET_4_11), .out(_11_2), .sel(ADDRESS[3:2]));  // open: en
  or or_10 (or_10_out, LIN_1_SET_1_FILTER, LIN_2_SET_1_FILTER);
  or or_11 (or_11_out, LIN_1_SET_2_FILTER, LIN_2_SET_2_FILTER);
  or or_12 (or_12_out, LIN_1_SET_3_FILTER, LIN_2_SET_3_FILTER);
  or or_13 (or_13_out, LIN_1_SET_4_FILTER, LIN_2_SET_4_FILTER);
  and and_49 (and_49_out, comparator_9_eq, V1_1_SET_1);
  and and_50 (and_50_out, comparator_10_eq, V2_1_SET_1);
  and and_51 (and_51_out, comparator_11_eq, V1_1_SET_2);
  and and_52 (and_52_out, comparator_12_eq, V2_1_SET_2);
  and and_53 (and_53_out, comparator_13_eq, V1_1_SET_3);
  and and_54 (and_54_out, comparator_14_eq, V2_1_SET_3);
  and and_55 (and_55_out, comparator_15_eq, V1_1_SET_4);
  and and_56 (and_56_out, comparator_16_eq, V2_1_SET_4);
  or or_14 (or_14_out, str_lin_1_set_1, str_lin_2_set_1);
  or or_15 (or_15_out, str_lin_1_set_2, str_lin_2_set_2);
  or or_16 (or_16_out, str_lin_1_set_3, str_lin_2_set_3);
  or or_17 (or_17_out, str_lin_1_set_4, str_lin_2_set_4);
  or or_18 (or_18_out, M1_LIN_1, M2_LIN_2);
  or or_19 (or_19_out, M1_LIN_1, M2_LIN_2);
  or or_20 (or_20_out, M3_LIN_1, M3_LIN_2);
  or or_21 (or_21_out, M4_LIN_1, M4_LIN_2);
  assign TAG_SET_1 = LIN_1_SET_1_FILTER ? TAG_1_SET_1 : 6'bz;  // Controlled_Buffer controlled_buffer_41
  assign TAG_SET_1 = LIN_2_SET_1_FILTER ? TAG_2_SET_1 : 6'bz;  // Controlled_Buffer controlled_buffer_42
  assign TAG_SET_2 = LIN_1_SET_2_FILTER ? TAG_1_SET_2 : 6'bz;  // Controlled_Buffer controlled_buffer_43
  assign TAG_SET_2 = LIN_2_SET_2_FILTER ? TAG_2_SET_2 : 6'bz;  // Controlled_Buffer controlled_buffer_44
  assign TAG_SET_3 = LIN_1_SET_3_FILTER ? TAG_1_SET_3 : 6'bz;  // Controlled_Buffer controlled_buffer_45
  assign TAG_SET_3 = LIN_2_SET_3_FILTER ? TAG_2_SET_3 : 6'bz;  // Controlled_Buffer controlled_buffer_46
  assign TAG_SET_4 = LIN_1_SET_4_FILTER ? TAG_1_SET_4 : 6'bz;  // Controlled_Buffer controlled_buffer_47
  assign TAG_SET_4 = LIN_2_SET_4_FILTER ? TAG_2_SET_4 : 6'bz;  // Controlled_Buffer controlled_buffer_48
  and and_57 (and_57_out, or_10_out, miss_1);
  and and_58 (and_58_out, miss_2, or_11_out);
  and and_59 (and_59_out, miss_3, or_12_out);
  and and_60 (and_60_out, miss_4, or_13_out);
  Multiplexer #(.width(16)) multiplexer_5 (
    .in0(WORD_1_SET_1), .in1(WORD_2_SET_1), .out(set_1), .sel(and_61_out));  // open: en
  and and_61 (and_61_out, ~and_49_out, and_50_out);  // AND_Gate
  or or_22 (or_22_out, and_49_out, and_50_out);
  Multiplexer #(.width(16)) multiplexer_6 (
    .in0(WORD_1_SET_2), .in1(WORD_2_SET_2), .out(set_2), .sel(and_62_out));  // open: en
  and and_62 (and_62_out, ~and_51_out, and_52_out);  // AND_Gate
  or or_23 (or_23_out, and_51_out, and_52_out);
  Multiplexer #(.width(16)) multiplexer_7 (
    .in0(WORD_1_SET_3), .in1(WORD_2_SET_3), .out(set_3), .sel(and_63_out));  // open: en
  and and_63 (and_63_out, ~and_53_out, and_54_out);  // AND_Gate
  or or_24 (or_24_out, and_53_out, and_54_out);
  Multiplexer #(.width(16)) multiplexer_8 (
    .in0(WORD_1_SET_4), .in1(WORD_2_SET_4), .out(set_4), .sel(and_64_out));  // open: en
  and and_64 (and_64_out, ~and_55_out, and_56_out);  // AND_Gate
  or or_25 (or_25_out, and_55_out, and_56_out);
  Multiplexer #(.select(2)) multiplexer_9 (
    .in0(or_14_out), .in1(or_15_out), .in2(or_16_out), .in3(or_17_out), .out(multiplexer_9_out),
    .sel(ADDRESS[3:2]));  // open: en
  Multiplexer #(.select(2)) multiplexer_10 (
    .in0(or_18_out), .in1(or_19_out), .in2(or_20_out), .in3(or_21_out), .out(multiplexer_10_out),
    .sel(ADDRESS[3:2]));  // open: en
  Multiplexer #(.select(2)) multiplexer_11 (
    .in0(and_57_out), .in1(and_58_out), .in2(and_59_out), .in3(and_60_out), .out(multiplexer_11_out),
    .sel(ADDRESS[3:2]));  // open: en
  and and_65 (and_65_out, or_22_out, set1);
  Multiplexer multiplexer_12 (.in0(INS_1_SET_2), .in1(INS_2_SET_2), .out(ins_set_2), .sel(and_62_out));  // open: en
  and and_66 (and_66_out, or_23_out, set2);
  and and_67 (and_67_out, or_24_out, set3);
  Multiplexer multiplexer_13 (.in0(INS_1_SET_3), .in1(INS_2_SET_3), .out(ins_set_3), .sel(and_63_out));  // open: en
  Multiplexer multiplexer_14 (.in0(INS_1_SET_4), .in1(INS_2_SET_4), .out(ins_set_4), .sel(and_64_out));  // open: en
  and and_68 (and_68_out, multiplexer_9_out, multiplexer_10_out);
  Multiplexer multiplexer_15 (.in0(INS_1_SET_1), .in1(INS_2_SET_1), .out(ins_set_1), .sel(and_61_out));  // open: en
  and and_69 (and_69_out, set4, or_25_out);
  Register #(.width(1)) register_5 (.D(and_68_out), .en(1'b1), .Q(MODIFIED), .clk(CLOCK), .clr(CLEAR));
  and and_70 (WRITE_BACK, multiplexer_11_out, ~HIT);  // AND_Gate
  _4_1MUX u_4_1mux_1 (.A(and_69_out), .B(and_67_out), .C(and_66_out), .D(and_65_out), .Z(INST[1]), .x(INST[0]));
  or or_26 (HIT, and_65_out, and_66_out, and_67_out, and_69_out);
  Multiplexer #(.select(2), .width(16)) multiplexer_16 (
    .in0(set_1), .in1(set_2), .in2(set_3), .in3(set_4), .out(DATA_TO_LOAD), .sel(INST), .en(HIT));
  or or_27 (or_27_out, 1'b0, LW);
  not not_9 (miss_1, and_65_out);
  not not_10 (miss_2, and_66_out);
  not not_11 (miss_3, and_67_out);
  not not_12 (miss_4, and_69_out);
  Multiplexer #(.select(2)) multiplexer_17 (
    .in0(ins_set_1), .in1(ins_set_2), .in2(ins_set_3), .in3(ins_set_4), .out(\INSTRUÇÃO ), .sel(INST));  // open: en
  Multiplexer #(.select(2), .width(10)) multiplexer_18 (
    .in0({TAG_SET_1, 4'b0000}), .in1({TAG_SET_2, 4'b0100}), .in2({TAG_SET_3, 4'b1000}),
    .in3({TAG_SET_4, 4'b1100}), .out(address_to_write), .sel(ADDRESS[3:2]));  // open: en
  // NOT_Gate not_13 is placed but not wired

  assign out_19 = ADDRESS;

  // Other names for the same wires on the sheet: CLK = CLOCK; DATA[15:0] = DATA_TO_STORE; hitizim = HIT;
  //   modificado = MODIFIED; addr[9:0] = ADDRESS; offset[1:0] = ADDRESS[1:0]; set[1:0] = ADDRESS[3:2]; STR_WORD = SW;
  //   tag[5:0] = ADDRESS[9:4]; wb = WRITE_BACK

  // Notes on the sheet:
  //   LRU
  //   LRU
  //   LRU
  //   LRU
endmodule

module linha_cache (
  input  [15:0] data_00,
  input  [15:0] data_01,
  input  [15:0] data_10,
  input  [15:0] data_11,
  input  [15:0] WORD,
  input  [1:0] offset,
  input  [5:0] tag,
  input  SW,
  input  clock,
  input  enable,
  input  LRU,
  input  CLEAR,
  input  store_word,
  input  block_saved,
  input  modificado,
  output [15:0] _00,
  output [15:0] _01,
  output [15:0] _10,
  output [15:0] _11,
  output [15:0] WORD_2,
  output [5:0] TAG_2,
  output V,
  output M,
  output LRU_2,
  output \INSTRUÇÃO 
);

  wire and_2_out, and_3_out, and_4_out, and_5_out, and_6_out, barra_1, barra_2, barra_3, barra_4, EN,
       not_1_out, not_2_out, or_2_out, or_3_out, up_modify;
  wire [15:0] _00_t, _01_t, _10_t, _11_t, demultiplexer_1_out0, demultiplexer_1_out1, demultiplexer_1_out2,
       demultiplexer_1_out3;

  not not_1 (not_1_out, store_word);
  assign _00_t = not_1_out ? data_00 : 16'bz;  // Controlled_Buffer controlled_buffer_1
  assign _01_t = not_1_out ? data_01 : 16'bz;  // Controlled_Buffer controlled_buffer_2
  assign _10_t = not_1_out ? data_10 : 16'bz;  // Controlled_Buffer controlled_buffer_3
  assign _11_t = not_1_out ? data_11 : 16'bz;  // Controlled_Buffer controlled_buffer_4
  or or_1 (EN, enable, store_word);
  and and_1 (up_modify, store_word, ~modificado);  // AND_Gate
  Demultiplexer #(.select(2), .width(16)) demultiplexer_1 (
    .out0(demultiplexer_1_out0), .out1(demultiplexer_1_out1), .out2(demultiplexer_1_out2),
    .out3(demultiplexer_1_out3), .in(WORD), .sel(offset), .en(store_word));
  Decoder #(.select(2)) decoder_1 (
    .out0(barra_1), .out1(barra_2), .out2(barra_3), .out3(barra_4), .sel(offset), .en(store_word));
  assign _00_t = and_2_out ? demultiplexer_1_out0 : 16'bz;  // Controlled_Buffer controlled_buffer_5
  assign _01_t = and_3_out ? demultiplexer_1_out1 : 16'bz;  // Controlled_Buffer controlled_buffer_6
  assign _10_t = and_4_out ? demultiplexer_1_out2 : 16'bz;  // Controlled_Buffer controlled_buffer_7
  assign _11_t = and_5_out ? demultiplexer_1_out3 : 16'bz;  // Controlled_Buffer controlled_buffer_8
  and and_2 (and_2_out, store_word, barra_1);
  and and_3 (and_3_out, store_word, barra_2);
  and and_4 (and_4_out, store_word, barra_3);
  and and_5 (and_5_out, store_word, barra_4);
  not not_2 (not_2_out, clock);
  or or_2 (or_2_out, tag[1], tag[2], tag[3], tag[4], tag[5]);
  and and_6 (and_6_out, EN, SW);
  Register #(.width(16)) register_1 (.D(_00_t), .en(EN), .Q(_00), .clk(not_2_out), .clr(CLEAR));
  Register #(.width(16)) register_2 (.D(_01_t), .en(EN), .Q(_01), .clk(not_2_out), .clr(CLEAR));
  Register #(.width(16)) register_3 (.D(_10_t), .en(EN), .Q(_10), .clk(not_2_out), .clr(CLEAR));
  Register #(.width(16)) register_4 (.D(_11_t), .en(EN), .Q(_11), .clk(not_2_out), .clr(CLEAR));
  Register #(.width(6)) register_5 (.D(tag), .en(EN), .Q(TAG_2), .clk(not_2_out), .clr(CLEAR));
  Register #(.width(1)) register_6 (.D(SW), .en(and_6_out), .Q(V), .clk(not_2_out), .clr(CLEAR));
  Register #(.width(1)) register_7 (.D(store_word), .en(up_modify), .Q(M), .clk(not_2_out), .clr(or_3_out));
  or or_3 (or_3_out, CLEAR, block_saved);
  Register #(.width(1)) register_8 (.D(LRU), .en(SW), .Q(LRU_2), .clk(not_2_out), .clr(CLEAR));
  Register #(.width(1)) register_9 (.D(or_2_out), .en(EN), .Q(\INSTRUÇÃO ), .clk(not_2_out), .clr(CLEAR));
  Multiplexer #(.select(2), .width(16)) multiplexer_1 (
    .in0(_00), .in1(_01), .in2(_10), .in3(_11), .out(WORD_2), .sel(offset));  // open: en

  // Other names for the same wires on the sheet: CLK = clock; lru_t = enable

  // Notes on the sheet:
  //   TAG
endmodule

module _4_1MUX (
  input  A,
  input  B,
  input  C,
  input  D,
  output Z,
  output x
);

  wire and_2_out, and_3_out, not_1_out, not_2_out, not_3_out, not_4_out, not_5_out, not_6_out;

  not not_1 (not_1_out, A);
  not not_2 (not_2_out, C);
  not not_3 (not_3_out, D);
  not not_4 (not_4_out, B);
  not not_5 (not_5_out, B);
  and and_1 (x, not_5_out, not_6_out);
  not not_6 (not_6_out, D);
  and and_2 (and_2_out, not_1_out, B, not_2_out, not_3_out);
  or or_1 (Z, and_2_out, and_3_out);
  and and_3 (and_3_out, A, not_4_out);
endmodule

module MP_paralela (
  input  [9:0] ADDRESS,
  input  [15:0] _00,
  input  [15:0] _01,
  input  [15:0] _10,
  input  [15:0] _11,
  input  SW,
  input  LW,
  input  SELECT,
  input  CLOCK,
  input  CLEAR,
  output [15:0] _00_2,
  output [15:0] _01_2,
  output [15:0] _10_2,
  output [15:0] _11_2,
  output BLOCK_SAVED
);

  wire and_1_out, and_2_out, and_3_out, and_4_out, not_1_out, not_2_out, not_3_out, not_4_out;

  and and_1 (and_1_out, LW, ~SW);  // AND_Gate
  not not_1 (not_1_out, CLOCK);
  and and_2 (and_2_out, LW, ~SW);  // AND_Gate
  not not_2 (not_2_out, CLOCK);
  and and_3 (and_3_out, LW, ~SW);  // AND_Gate
  not not_3 (not_3_out, CLOCK);
  and and_4 (and_4_out, LW, ~SW);  // AND_Gate
  not not_4 (not_4_out, CLOCK);
  Register #(.width(1), .trigger("falling")) register_1 (
    .D(SW), .en(SELECT), .Q(BLOCK_SAVED), .clk(CLOCK));  // open: clr
  RAM #(.addrWidth(10), .dataWidth(16), .bus("separate")) ram_1 (
    .addr({ADDRESS[9:2], 2'b00}), .din(_00), .data(_00_2), .str(SW), .sel(SELECT), .clk(not_1_out),
    .ld(and_2_out), .clr(CLEAR));
  RAM #(.addrWidth(10), .dataWidth(16), .bus("separate")) ram_2 (
    .addr({ADDRESS[9:2], 2'b01}), .din(_01), .data(_01_2), .str(SW), .sel(SELECT), .clk(not_2_out),
    .ld(and_3_out), .clr(CLEAR));
  RAM #(.addrWidth(10), .dataWidth(16), .bus("separate")) ram_3 (
    .addr({ADDRESS[9:2], 2'b10}), .din(_10), .data(_10_2), .str(SW), .sel(SELECT), .clk(not_3_out),
    .ld(and_4_out), .clr(CLEAR));
  RAM #(.addrWidth(10), .dataWidth(16), .bus("separate")) ram_4 (
    .addr({ADDRESS[9:2], 2'b11}), .din(_11), .data(_11_2), .str(SW), .sel(SELECT), .clk(not_4_out),
    .ld(and_1_out), .clr(CLEAR));
endmodule

module LRU (
  input  V1,
  input  V2,
  input  LRU_1,
  input  LRU_2,
  input  MISS,
  input  memWrite,
  output WAY_1,
  output WAY_2,
  output SW
);

  wire multiplexer_1_out, multiplexer_2_out, multiplexer_3_out, or_1_out;

  or or_1 (or_1_out, V1, V2);
  Multiplexer multiplexer_1 (.in0(LRU_2), .in1(LRU_1), .out(multiplexer_1_out), .sel(memWrite));  // open: en
  Multiplexer multiplexer_2 (.in0(LRU_1), .in1(LRU_2), .out(multiplexer_2_out), .sel(memWrite));  // open: en
  Multiplexer multiplexer_3 (.in0(1'b1), .in1(multiplexer_1_out), .out(multiplexer_3_out), .sel(or_1_out));  // open: en
  and and_1 (WAY_1, MISS, multiplexer_3_out);
  and and_2 (WAY_2, MISS, multiplexer_2_out);
  or or_2 (SW, WAY_2, WAY_1);
endmodule

module CACHE_CONTROLLER (
  input  SW,
  input  LW,
  input  HIT,
  input  WRITE_BACK,
  input  in_5,
  output stall,
  output memRead,
  output memWrite,
  output cache_read,
  output cache_write
);

  not not_1 (memRead, HIT);
  or or_1 (stall, in_5, memRead);
  Multiplexer multiplexer_1 (.in0(WRITE_BACK), .in1(1'b0), .out(memWrite), .sel(in_5));  // open: en
  and and_1 (cache_read, HIT, LW);
  and and_2 (cache_write, SW, HIT);

  // Other names for the same wires on the sheet: BLOCK_SAVED = in_5; WB = WRITE_BACK
endmodule

module Main_Arq2 (
  input  select,
  input  clear,
  input  enable
);

  wire BLOCK_SAVED, button_1_out, cache_read, cache_write, clk_off, clock, clock_1_out, counter_1_carry, HIT,
       \INSTRUÇÃO_ENABLE , lw, mem_read, mem_write, MODIFICADO, not_1_out, not_2_out, not_3_out, or_1_out,
       or_2_out, stall, start, sw, write_back;
  wire [3:0] counter_2_q, counter_2_q_2, counter_3_q, counter_3_q_2, counter_3_q_3, counter_4_q_2,
       counter_4_q_3;
  wire [9:0] ADDRESS_WRITE, ADRESS, multiplexer_3_out;
  wire [11:8] counter_4_q;
  wire [15:0] _00, _00_s, _01, _01_s, _10, _10_s, _11, _11_s, DATA_LOAD, DATA_STORE;

  Multiplexer multiplexer_1 (.in0(1'b1), .in1(1'b0), .out(start), .sel(counter_1_carry));  // open: en
  Counter #(.width(4), .max('h4), .ongoal("stay"), .trigger("falling")) counter_1 (
    .count(select), .carry(counter_1_carry), .clk(clock), .clr(clear));  // open: load, D, Q
  LED led_1 (.in(HIT));
  CACHE_CONTROLLER cache_controller_1 (
    .SW(sw), .LW(lw), .HIT(HIT), .WRITE_BACK(write_back), .memRead(mem_read), .memWrite(mem_write),
    .stall(stall), .cache_read(cache_read), .cache_write(cache_write), .in_5(BLOCK_SAVED));
  not not_1 (not_1_out, clk_off);
  Clock clock_1 (.out(clock_1_out));
  Multiplexer multiplexer_2 (.in0(clock_1_out), .in1(1'b0), .out(clock), .sel(not_1_out));  // open: en
  processador_arq2 processador_arq2_1 (
    .LW(DATA_LOAD), .STALL(stall), .CLOCK(clock), .CLEAR(clear), .SELECT(select), .ENABLE(enable),
    .SW(DATA_STORE), .ADDRESS(ADRESS), .memRead(lw), .memWrite(sw), .start(start),
    .INSTRUCTIONS_ENABLE(\INSTRUÇÃO_ENABLE ), .MODIFICADO(MODIFICADO), .clk_off(clk_off));
  or or_1 (or_1_out, ADRESS[5], ADRESS[6], ADRESS[7], ADRESS[8], ADRESS[9]);
  or or_2 (or_2_out, lw, sw, or_1_out);
  cache cache_1 (
    .ADDRESS(ADRESS), ._00(_00_s), ._01(_01_s), ._10(_10_s), ._11(_11_s), .DATA_TO_STORE(DATA_STORE),
    .SW(cache_write), .LW(cache_read), .CLOCK(clock), .CLEAR(clear), ._00_2(_00), ._01_2(_01), ._10_2(_10),
    ._11_2(_11), .WRITE_BACK(write_back), .DATA_TO_LOAD(DATA_LOAD), .HIT(HIT),
    .\INSTRUÇÃO (\INSTRUÇÃO_ENABLE ), .MODIFIED(MODIFICADO), .address_to_write(ADDRESS_WRITE),
    .block_saved(BLOCK_SAVED));  // open: out_19
  LED led_2 (.in(HIT));
  Counter counter_2 (
    .count(not_2_out), .Q({counter_2_q, counter_2_q_2}), .clk(clock), .clr(clear));  // open: load, D, carry
  not not_2 (not_2_out, HIT);
  Counter #(.width(12), .max('hfff)) counter_3 (
    .count(HIT), .Q({counter_3_q, counter_3_q_2, counter_3_q_3}), .clk(clock), .clr(clear));  // open: load, D, carry
  Counter #(.width(12), .max('hfff)) counter_4 (
    .count(or_2_out), .Q({counter_4_q, counter_4_q_2, counter_4_q_3}), .clk(clock), .clr(clear));  // open: load, D, carry
  Hex_Digit_Display hex_digit_display_1 (.value(counter_2_q));  // open: dp
  Multiplexer #(.width(10)) multiplexer_3 (
    .in0(ADDRESS_WRITE), .in1(ADRESS), .out(multiplexer_3_out), .sel(not_3_out));  // open: en
  not not_3 (not_3_out, mem_write);
  Hex_Digit_Display hex_digit_display_2 (.value(counter_2_q_2));  // open: dp
  Hex_Digit_Display hex_digit_display_3 (.value(counter_3_q));  // open: dp
  Hex_Digit_Display hex_digit_display_4 (.value(counter_3_q_2));  // open: dp
  Hex_Digit_Display hex_digit_display_5 (.value(counter_4_q));  // open: dp
  Hex_Digit_Display hex_digit_display_6 (.value(counter_4_q_2));  // open: dp
  Button button_1 (.out(button_1_out));
  Hex_Digit_Display hex_digit_display_7 (.value(counter_3_q_3));  // open: dp
  Hex_Digit_Display hex_digit_display_8 (.value(counter_4_q_3));  // open: dp
  MP_paralela mp_paralela_1 (
    .ADDRESS(multiplexer_3_out), ._00(_00), ._01(_01), ._10(_10), ._11(_11), .SW(mem_write), .LW(mem_read),
    .SELECT(select), .CLOCK(clock), .CLEAR(button_1_out), ._00_2(_00_s), ._01_2(_01_s), ._10_2(_10_s),
    ._11_2(_11_s), .BLOCK_SAVED(BLOCK_SAVED));

  // Notes on the sheet:
  //   HIT
endmodule
